# Fritzing sketch Sound Sensor (saved by Fritzing 0.9.3b)
breadboards: 1

parts:
  Part2 = Arduino Nano (Rev3.0) (ICSP)
  LED5 = smd LED [color="Green (555nm)" package="0603 [SMD]"]
  R4 = Resistor [tolerance=±5% resistance=220 package="0603 [SMD]"]
  R5 = Resistor [tolerance=±5% resistance=220 package="0603 [SMD]"]
  Part3 = Breakout Board for Electret Microphone
  LED6 = smd LED [color="Red (635nm)" package="0603 [SMD]"]

nets:
  GND: Part2.GND, LED5.cathode, R5.Pin_0, Part3.GND, LED6.cathode
  N1: Part2.D4, R4.Pin_1, R5.Pin_1
  N2: Part2.5V, Part3.AUD
  N3: Part2.A2, Part3.VCC
  N4: LED5.anode, R4.Pin_0

// code stored in the sketch: Sensor.ino

/**************************************************************************/
/*!
Sound Sensor
*/
/**************************************************************************/

int soundSensor=A2;												// Set analog pin 2 for receiving analog sound data
int GreenLED = 3;													// Set digital pin 3 as green LED output
int RedLED = 4;														// Set digital pin 3 as red LED output
int SoundOffset = 60;											// Set noise offset to 0 data (offset determined using Serial Plotter)
boolean GreenLEDStatus = true;							// Set green LED to on
boolean RedLEDStatus = false;							// Set red LED to off

void setup() {
 pinMode(soundSensor,INPUT);								// Set temperature sensor as an input
 pinMode(GreenLED,OUTPUT);									// Set green LED as an output
 pinMode(RedLED,OUTPUT);										// Set red LED as an output
 Serial.begin(9600);												//

}

void loop() {

  int SensorData=analogRead(soundSensor);		// Read sound
  int SensorData2 = SensorData-Offset;			// Subtract offset (determined from Serial Plotter)
  int SoundThreshold = 2;									// Set arbitrary sound threshold to change LED outputs
  
  Serial.println();
  Serial.print(SensorData2); 							// Print sound data

  if(SensorData2>SoundThreshold){					// If sound exceeds threshold, switch green LED off and red LED on

    GreenLEDStatus=false;
    RedLEDStatus=true;
    digitalWrite(GreenLED,LOW);
    digitalWrite(RedLED,HIGH);
    }
  else{
    RedLEDStatus=false;										// If sound drops below threshold, switch rred LED off and green LED on
    GreenLEDStatus=true;
    digitalWrite(GreenLED,HIGH);
    digitalWrite(RedLED,LOW);
    }
  }
